# Fritzing sketch Arduino WireUp (saved by Fritzing 0.9.2b)
breadboards: 1

parts:
  Onderdeel1 = Arduino Uno (Rev3) - ICSP
  U1 = Voltage Regulator - 5V [package="TO220 [THT]"]

nets:
  N1: Onderdeel1.5V, U1.input_voltage

notes:
  To Roomba
  To Pin 3 (RX)
  To Pin 1 or 2 (Vpwr)
  To pin 6 or 7 (GND)
